# Fritzing sketch HIIT_Timer_Arduino (saved by Fritzing 0.9.3b)
breadboards: 1

parts:
  Part1 = Arduino Uno (Rev3)
  LCD1 = LCD screen
  R1 = Trimmer Potentiometer [maximum_resistance=10kΩ package=THT]
  J1 = Piezo Speaker
  S1 = Pushbutton [package="[THT]"]
  R2 = Resistor [tolerance=±5% resistance=220 package=THT]
  LED1 = LED - 3mm [color="Blue (430nm)" package="3 mm [THT]"]

nets:
  N1: Part1.D9_PWM, R2.Pin_0
  GND: Part1.D10_PWM/SS, Part1.GND, LCD1.VSS, LCD1.R/W, LCD1.LED-, R1.leg2, J1.pin1, S1.Pin_3, S1.Pin_4, LED1.cathode
  N2: Part1.D11_PWM/MOSI, LCD1.E
  N3: Part1.D12/MISO, LCD1.RS
  N4: Part1.D2, LCD1.DB7
  N5: Part1.D3_PWM, LCD1.DB6
  N6: Part1.D4, LCD1.DB5
  N7: Part1.D5_PWM, LCD1.DB4
  5V: Part1.5V, LCD1.VDD, LCD1.LED+, R1.leg1
  N8: LCD1.V0, R1.wiper
  N9: J1.pin2, R2.Pin_1, LED1.anode
